// Logisim project _main.circ as structural Verilog: 2 circuits, main circuit main
module main (
);

  wire alu_1_p1, alu_1_p2, alu_1_p7, and_1_out, button_1_out, clock_1_out, clock_2_out, DECODE_ENABLE,
       EXECUTE_ENABLE, FETCH_ENABLE, instruction_memory_1_p3, instruction_memory_1_p4,
       instruction_memory_1_p5, instruction_memory_1_p6, memory_controller_1_read_enable,
       memory_controller_1_write_enable, MEMORY_ENABLE, not_1_out, RAM_LOAD_ENABLE, RAM_STORE_ENABLE,
       rom_loader_1_ioenable, WRITEBACK_ENABLE;
  wire [2:0] counter_1_q;
  wire [3:0] instruction_memory_1_p2;
  wire [7:0] adder_1_out, instruction_memory_1_p7, RAM_ADDR, rom_loader_1_addrout;
  wire [23:0] RAM_DATA_IN, RAM_DATA_OUT, rom_loader_1_dataout;

  and and_1 (and_1_out, clock_1_out, not_1_out);
  Clock clock_1 (.out(clock_1_out));
  Button button_1 (.out(button_1_out));
  Counter #(.width(3), .max('h4)) counter_1 (.Q(counter_1_q), .clk(and_1_out));  // open: load, D, count, carry, clr
  Decoder #(.select(3), .disabled(0)) decoder_1 (
    .out0(FETCH_ENABLE), .out1(DECODE_ENABLE), .out2(EXECUTE_ENABLE), .out3(MEMORY_ENABLE),
    .out4(WRITEBACK_ENABLE), .sel(counter_1_q), .en(not_1_out));  // open: out5, out6, out7
  not not_1 (not_1_out, RAM_STORE_ENABLE);
  ROM_loader rom_loader_1 (
    .RELOAD(button_1_out), .DATAOUT(rom_loader_1_dataout), .ADDROUT(rom_loader_1_addrout),
    .IOENABLE(rom_loader_1_ioenable));
  // Probe on RAM_ADDR
  // Probe on RAM_DATA_IN
  memory_controller memory_controller_1 (
    .read_enable(memory_controller_1_read_enable), .write_enable(memory_controller_1_write_enable),
    .icode(instruction_memory_1_p2));
  assign RAM_LOAD_ENABLE = FETCH_ENABLE ? memory_controller_1_read_enable : 1'bz;  // Controlled_Buffer controlled_buffer_1
  assign RAM_STORE_ENABLE = FETCH_ENABLE ? memory_controller_1_write_enable : 1'bz;  // Controlled_Buffer controlled_buffer_2
  assign RAM_ADDR = rom_loader_1_ioenable ? rom_loader_1_addrout : 8'bz;  // Controlled_Buffer controlled_buffer_3
  assign RAM_DATA_IN = rom_loader_1_ioenable ? rom_loader_1_dataout : 24'bz;  // Controlled_Buffer controlled_buffer_4
  assign RAM_STORE_ENABLE = rom_loader_1_ioenable ? rom_loader_1_ioenable : 1'bz;  // Controlled_Buffer controlled_buffer_5
  // instruction_memory instruction_memory_1: pin names not known; wires that end beside it: FETCH_ENABLE, instruction_memory_1_p2, instruction_memory_1_p3, instruction_memory_1_p4, instruction_memory_1_p5, instruction_memory_1_p6, instruction_memory_1_p7
  Adder adder_1 (.a(instruction_memory_1_p7), .b(8'h1), .out(adder_1_out));  // open: cin, cout
  // ALU alu_1: pin names not known; wires that end beside it: alu_1_p1, alu_1_p2, instruction_memory_1_p6, alu_1_p1, alu_1_p2, instruction_memory_1_p3, alu_1_p7
  // _6x8_Register_File 6x8_register_file_1: pin names not known; wires that end beside it: instruction_memory_1_p4, instruction_memory_1_p5, alu_1_p1, alu_1_p7, instruction_memory_1_p5, instruction_memory_1_p4
  Clock clock_2 (.out(clock_2_out));
  RAM #(.dataWidth(24), .bus("separate")) ram_1 (
    .addr(RAM_ADDR), .din(RAM_DATA_IN), .data(RAM_DATA_OUT), .str(RAM_STORE_ENABLE), .clk(clock_2_out),
    .ld(RAM_LOAD_ENABLE));  // open: sel, clr

  // Notes on the sheet:
  //   ioeajsrjeaior
endmodule

module instruction_memory (
  input  ENABLE,
  input  [7:0] NEWPC,
  output [3:0] ICODE,
  output [3:0] IFUN,
  output [3:0] rA,
  output [3:0] rB,
  output [7:0] valC,
  output [7:0] PC
);

  wire clock_1_out;

  Register register_1 (.D(NEWPC), .en(ENABLE), .Q(PC), .clk(clock_1_out));  // open: clr
  Clock clock_1 (.out(clock_1_out));

  // Other names for the same wires on the sheet: RAM_ADDR[7:0] = PC; RAM_DATA_OUT[23:0] = {valC, rB, rA, IFUN, ICODE};
  //   RAM_LOAD_ENABLE = ENABLE

  // Notes on the sheet:
  //   ENABLE: pull=down
endmodule
