// Logisim project pc_increment_logic.circ as structural Verilog: 1 circuit, main circuit pc_increment_jump_controller
module pc_increment_jump_controller (
  input  [3:0] ifun,
  input  [3:0] icode,
  input  [1:0] FLAG,
  input  [7:0] ValC,
  output [7:0] PC_Increment_Final_Output
);

  wire comparator_1_eq;
  wire [3:0] multiplexer_8_out;
  wire [7:0] multiplexer_1_out, multiplexer_3_out, multiplexer_4_out, multiplexer_5_out, multiplexer_6_out,
       multiplexer_7_out;

  Multiplexer #(.select(2), .width(8), .enable("false")) multiplexer_1 (
    .in0(8'h1), .in1(ValC), .in2(ValC), .in3(8'h1), .out(multiplexer_1_out), .sel(FLAG));
  Multiplexer #(.select(4), .width(8), .enable("false")) multiplexer_2 (
    .in0(ValC), .in1(multiplexer_1_out), .in2(multiplexer_3_out), .in3(multiplexer_4_out),
    .in4(multiplexer_5_out), .in5(multiplexer_6_out), .in6(multiplexer_7_out), .in7(8'h1), .in8(8'h1),
    .in9(8'h1), .in10(8'h1), .in11(8'h1), .in12(8'h1), .in13(8'h1), .in14(8'h1), .in15(8'h1),
    .out(PC_Increment_Final_Output), .sel(multiplexer_8_out));
  Multiplexer #(.select(2), .width(8), .enable("false")) multiplexer_3 (
    .in0(8'h1), .in1(ValC), .in2(8'h1), .in3(8'h1), .out(multiplexer_3_out), .sel(FLAG));
  Multiplexer #(.select(2), .width(8), .enable("false")) multiplexer_4 (
    .in0(8'h1), .in1(8'h1), .in2(ValC), .in3(8'h1), .out(multiplexer_4_out), .sel(FLAG));
  Multiplexer #(.select(2), .width(8), .enable("false")) multiplexer_5 (
    .in0(ValC), .in1(ValC), .in2(8'h1), .in3(8'h1), .out(multiplexer_5_out), .sel(FLAG));
  Multiplexer #(.select(2), .width(8), .enable("false")) multiplexer_6 (
    .in0(ValC), .in1(8'h1), .in2(8'h1), .in3(8'h1), .out(multiplexer_6_out), .sel(FLAG));
  Multiplexer #(.select(2), .width(8), .enable("false")) multiplexer_7 (
    .in0(ValC), .in1(8'h1), .in2(ValC), .in3(8'h1), .out(multiplexer_7_out), .sel(FLAG));
  Multiplexer #(.width(4), .enable("false")) multiplexer_8 (
    .in0(4'b0111), .in1(ifun), .out(multiplexer_8_out), .sel(comparator_1_eq));
  Comparator #(.width(4)) comparator_1 (.a(icode), .b(4'b1001), .eq(comparator_1_eq));  // open: gt, lt
endmodule
