// Logisim project rom-ram.circ as structural Verilog: 1 circuit, main circuit ROM_loader
module ROM_loader (
  input  RELOAD,
  output [31:0] DATAOUT,
  output [7:0] ADDROUT,
  output IOENABLE
);

  wire clock_1_out, counter_1_carry, not_1_out;

  Counter counter_1 (
    .count(not_1_out), .Q(ADDROUT), .carry(counter_1_carry), .clk(clock_1_out), .clr(RELOAD));  // open: load, D
  not not_1 (not_1_out, counter_1_carry);
  Clock clock_1 (.out(clock_1_out));
  not not_2 (IOENABLE, counter_1_carry);
  ROM #(.dataWidth(32)) rom_1 (.addr(ADDROUT), .data(DATAOUT));  // open: sel

  // Notes on the sheet:
  //   contents of rom_1 (hex, n*v repeats v):
  //   256*11
endmodule
